// Logisim project Projet.circ as structural Verilog
module Add8bits (
  input  [7:0] in_1,
  input  [7:0] in_2,
  output [7:0] out_3,
  output ZF,
  output CF,
  output SF,
  output OF
);

  wire and_1_out, and_2_out, comparator_1_lt, comparator_2_lt, not_1_out, not_2_out, not_3_out, or_1_out;

  Adder adder_1 (.a(in_1), .b(in_2), .out(out_3));  // open: cin, cout
  Subtractor subtractor_1 (.a(in_1), .b(in_2), .out(out_3));  // open: bin, bout
  not not_1 (not_1_out, in_2[7]);
  not not_2 (not_2_out, in_1[7]);
  // NOT_Gate not_3 has open pins: in=open, out=not_3_out
  Comparator comparator_1 (.a(out_3), .b(in_1), .lt(comparator_1_lt));  // open: gt, eq
  Comparator comparator_2 (.a(out_3), .b(in_2), .lt(comparator_2_lt));  // open: gt, eq
  and and_1 (and_1_out, in_2[7], not_3_out, in_1[7]);
  and and_2 (and_2_out, not_1_out, not_2_out);
  not not_4 (ZF, or_1_out);
  or or_1 (or_1_out, out_3[0], out_3[1], out_3[2], out_3[3], out_3[4], out_3[5], out_3[6], out_3[7]);
  or or_2 (OF, and_1_out, and_2_out);
  or or_3 (CF, comparator_1_lt, comparator_2_lt);
  not not_5 (SF, 1'b1);
endmodule

module Soustracteur8bits (
  input  [7:0] in_1,
  input  [7:0] in_2,
  output [7:0] out_3
);

  Subtractor subtractor_1 (.a(in_1), .b(in_2), .out(out_3));  // open: bin, bout
endmodule

module OU8bits (
  input  [7:0] in_1,
  input  [7:0] in_2,
  output [7:0] out_3,
  output ZF
);

  wire or_2_out;
  wire [7:0] subtractor_1_out;

  assign out_3 = in_1 | in_2;  // OR_Gate or_1, 8 bits wide
  Subtractor subtractor_1 (.a(in_1), .b(in_2), .out(subtractor_1_out));  // open: bin, bout
  or or_2 (or_2_out, subtractor_1_out[0], subtractor_1_out[1], subtractor_1_out[2], subtractor_1_out[3], subtractor_1_out[4], subtractor_1_out[5], subtractor_1_out[6], subtractor_1_out[7]);
  not not_1 (ZF, or_2_out);
endmodule

module UAL (
  input  [7:0] RS,
  input  [7:0] RT,
  input  [2:0] in_3,
  output CF,
  output ZF,
  output SF,
  output OF,
  output [7:0] out_8
);

  wire and_1_out, and_2_out, and_3_out, and_5_out;
  wire [7:0] adder_1_out, and_4_out, not_1_out, or_1_out, shifter_1_out, shifter_2_out, subtractor_1_out;

  Subtractor subtractor_1 (.a(RS), .b(RT), .out(subtractor_1_out));  // open: bin, bout
  Adder adder_1 (.a(RS), .b(RT), .out(adder_1_out), .cout(CF));  // open: cin
  and and_1 (and_1_out, ~out_8[7], RS[7], ~RT[7], in_3[0]);  // AND_Gate
  assign or_1_out = RT | RS;  // OR_Gate or_1, 8 bits wide
  and and_2 (and_2_out, ~out_8[7], RS[7], RT[7], ~in_3[0]);  // AND_Gate
  Multiplexer #(.select(3), .width(8)) multiplexer_1 (
    .in0(adder_1_out), .in1(subtractor_1_out), .in2(or_1_out), .in3(and_4_out), .in4(not_1_out),
    .in5(shifter_1_out), .in6(shifter_2_out), .out(out_8), .sel(in_3));  // open: in7, en
  and and_3 (and_3_out, out_8[7], ~RS[7], ~RT[7], ~in_3[0]);  // AND_Gate
  or or_2 (OF, and_1_out, and_2_out, and_3_out, and_5_out);
  assign not_1_out = ~RS;  // NOT_Gate not_1, 8 bits wide
  assign and_4_out = RT & RS;  // AND_Gate and_4, 8 bits wide
  and and_5 (and_5_out, out_8[7], ~RS[7], RT[7], in_3[0]);  // AND_Gate
  Shifter shifter_1 (.in(RS), .\dist (RT[2:0]), .out(shifter_1_out));
  Shifter #(.shift("lr")) shifter_2 (.in(RS), .\dist (RT[2:0]), .out(shifter_2_out));
  and and_6 (ZF, ~out_8[0], ~out_8[1], ~out_8[2], ~out_8[3], ~out_8[4], ~out_8[5], ~out_8[6], ~out_8[7]);  // AND_Gate

  assign SF = out_8[7];
endmodule

module decoder_instru (
  input  [3:0] in_1,
  output isJMP,
  output regWrite,
  output isLoad,
  output [2:0] ctrlUAL
);

  wire and_1_out, and_2_out, and_3_out, or_1_out;

  and and_1 (and_1_out, in_1[3], ~in_1[2]);  // AND_Gate
  and and_2 (and_2_out, in_1[3], in_1[2], ~in_1[1]);  // AND_Gate
  and and_3 (and_3_out, in_1[3], in_1[1], ~in_1[0]);  // AND_Gate
  or or_1 (or_1_out, and_3_out, and_2_out, and_1_out);
  and and_4 (isLoad, in_1[3], in_1[2], in_1[1], in_1[0]);
  Multiplexer #(.width(3)) multiplexer_1 (.in0(3'b001), .in1(in_1[2:0]), .out(ctrlUAL), .sel(or_1_out));  // open: en
  not not_1 (isJMP, in_1[3]);

  assign regWrite = in_1[3];
endmodule

module CtrlSaut (
  input  CF,
  input  ZF,
  input  SF,
  input  OF,
  input  [3:0] opcode,
  output [1:0] out_6
);

  wire and_1_out, and_2_out, and_3_out, and_4_out, and_5_out, and_6_out, and_7_out, and_8_out, halt_out,
       or_2_out, or_3_out;
  wire [1:1] or_1_out;

  and and_1 (and_1_out, ~ZF, ~opcode[2], opcode[1], ~opcode[0]);  // AND_Gate
  and and_2 (and_2_out, ZF, ~opcode[2], opcode[1], opcode[0]);  // AND_Gate
  and and_3 (and_3_out, opcode[2], ~opcode[1], ~opcode[0], ~ZF, SF);  // AND_Gate
  or or_1 (or_1_out[1], and_1_out, and_2_out, and_3_out, and_4_out, and_5_out, and_7_out, ~opcode[3]);  // OR_Gate
  and and_4 (and_4_out, opcode[2], ~opcode[1], opcode[0], ~ZF, ~SF);  // AND_Gate
  and and_5 (and_5_out, opcode[2], ~opcode[1], opcode[0], or_2_out);  // AND_Gate
  and and_6 (and_6_out, ~ZF, SF);  // AND_Gate
  or or_2 (or_2_out, and_6_out, ZF);
  and and_7 (and_7_out, opcode[2], opcode[1], opcode[0], or_3_out);
  and and_8 (and_8_out, ~ZF, ~SF);  // AND_Gate
  or or_3 (or_3_out, and_8_out, ZF);
  and halt (halt_out, ~opcode[3], ~opcode[2], ~opcode[1], ~opcode[0]);  // AND_Gate
  Multiplexer #(.width(2)) multiplexer_1 (
    .in0({or_1_out[1], 1'b1}), .in1(2'b00), .out(out_6), .sel(halt_out));  // open: en
endmodule
