// Logisim project controlSaut.circ as structural Verilog: 1 circuit, main circuit main
module main (
  input  SF,
  input  ZF,
  input  [3:0] opcode,
  output [1:0] nextPCselect
);

  wire and_1_out, and_2_out, and_3_out, and_4_out, and_5_out, and_6_out, and_7_out, and_8_out, HALT_out,
       or_2_out, or_3_out;
  wire [1:1] or_1_out;

  and and_1 (and_1_out, ~ZF, ~opcode[2], opcode[1], ~opcode[0]);  // AND_Gate
  and and_2 (and_2_out, ZF, ~opcode[2], opcode[1], opcode[0]);  // AND_Gate
  and and_3 (and_3_out, opcode[2], ~opcode[1], ~opcode[0], ~ZF, SF);  // AND_Gate
  or or_1 (or_1_out[1], and_1_out, and_2_out, and_3_out, and_4_out, and_5_out, and_7_out, ~opcode[3]);  // OR_Gate
  and and_4 (and_4_out, opcode[2], ~opcode[1], opcode[0], ~ZF, ~SF);  // AND_Gate
  and and_5 (and_5_out, opcode[2], ~opcode[1], opcode[0], or_2_out);  // AND_Gate
  and and_6 (and_6_out, ~ZF, SF);  // AND_Gate
  or or_2 (or_2_out, and_6_out, ZF);
  and and_7 (and_7_out, opcode[2], opcode[1], opcode[0], or_3_out);
  and and_8 (and_8_out, ~ZF, ~SF);  // AND_Gate
  or or_3 (or_3_out, and_8_out, ZF);
  and HALT (HALT_out, ~opcode[3], ~opcode[2], ~opcode[1], ~opcode[0]);  // AND_Gate
  Multiplexer #(.width(2)) multiplexer_1 (
    .in0({or_1_out[1], 1'b1}), .in1(2'b00), .out(nextPCselect), .sel(HALT_out));  // open: en

  // Notes on the sheet:
  //   Cédric Bois,  Sientzoff - Contrôleur de saut
endmodule
