// Logisim project selectRegistres.circ as structural Verilog: 1 circuit, main circuit main
module main (
  input  [3:0] Rd,
  input  [3:0] Rs,
  input  [3:0] Rt,
  input  isJump,
  output [3:0] Rs_Rt,
  output [3:0] Rd_Rt,
  output [3:0] RD_2
);

  Multiplexer #(.width(4)) multiplexer_1 (.in0(Rd), .in1(Rs), .out(Rd_Rt), .sel(isJump));  // open: en
  Multiplexer #(.width(4)) multiplexer_2 (.in0(Rs), .in1(Rt), .out(Rs_Rt), .sel(isJump));  // open: en

  assign RD_2 = Rd;

  // Notes on the sheet:
  //   Cédric Bois,  Sientzoff - Sélection de registres
endmodule
